# Fritzing sketch ESP32 (saved by Fritzing 0.9.3b)
breadboards: 1

parts:
  esp1 = ESP32 DevKitc V4
  Mod1 = KY-019 5V Relay Module [package="Breakout board"]
  Componente1 = RFID-RC522-v2
  LED1 = smd LED [color="Red (633nm)" package="0805 [SMD]"]
  LED2 = smd LED [color="Green (570nm)" package="0805 [SMD]"]

nets:
  N1: esp1.IO2, LED1.cathode
  N2: esp1.IO4, LED2.cathode
  N3: esp1.GND#18, Mod1.-, LED1.anode, LED2.anode
  3V3: esp1.3V3, Componente1.3.3V
  N4: esp1.IO33, Mod1.S
  N5: esp1.IO25, Componente1.RST
  N6: esp1.IO26, Componente1.SDA
  N7: esp1.IO27, Componente1.MOSI
  N8: esp1.IO14, Componente1.MISO
  N9: esp1.IO12, Componente1.SCK
  N10: esp1.GND#32, Componente1.GND
  N11: esp1.5V, Mod1.+

custom parts:
  ESP32 DevKitc V4: ESP32-DevKitC board with ESP32-WROOM-32 module. ESP32-DevKitC V4 is a small-sized ESP32-based development board produced by Espressif. Most of the pins on the ESP module are broken out to the pin headers on the board. The pins D0, D1, D2, D3, CMD and CLK are used internally for communication between ESP32 and SPI flash memory. They are grouped on both sides near the USB connector. Avoid using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
  KY-019 5V Relay Module: KY-019 5V Relay module, used to control AC circuits. (Special thanks to vanepp for fixing the PCB holes and other errors)
  RFID-RC522-v2: A simple China made RFID-RC522 Reader; do check the pin labels, as this is a MFRC522 based clone.
